# Fritzing sketch schema (saved by Fritzing 0.9.3b)
breadboards: 1

parts:
  WeMos_D1_Mini1 = WeMos D1 Mini
  WeMos_D1_Mini_WS2812B_RGB_Shield1 = WeMos D1 Mini WS2812B RGB Shield
  Componente1 = SHT1x-Breakout

nets:
  5V: WeMos_D1_Mini1.5V, WeMos_D1_Mini_WS2812B_RGB_Shield1.5V, Componente1.VCC
  N1: WeMos_D1_Mini1.D1, Componente1.DATA
  N2: WeMos_D1_Mini1.D2, Componente1.SCK
  N3: WeMos_D1_Mini1.D4, WeMos_D1_Mini_WS2812B_RGB_Shield1.D4
  N4: WeMos_D1_Mini1.G, WeMos_D1_Mini_WS2812B_RGB_Shield1.G, Componente1.GND
